// Digital circuit adv-1a.dig as structural Verilog
module adv_1a (
  input  A,
  input  B
);

  wire and_1_out, nand_1_out, nor_1_out, not_1_out, not_2_out, or_1_out, xnor_1_out, xor_1_out;

  not not_1 (not_1_out, A);
  not not_2 (not_2_out, B);
  and and_1 (and_1_out, A, B);
  or or_1 (or_1_out, A, B);
  xor xor_1 (xor_1_out, A, B);
  nand nand_1 (nand_1_out, A, B);
  nor nor_1 (nor_1_out, A, B);
  xnor xnor_1 (xnor_1_out, A, B);
  LED NOT_A (.in(not_1_out));
  LED NOT_B (.in(not_2_out));
  LED AND_2 (.in(and_1_out));
  LED OR_2 (.in(or_1_out));
  LED XOR_2 (.in(xor_1_out));
  LED NAND_2 (.in(nand_1_out));
  LED NOR_2 (.in(nor_1_out));
  LED XNOR_2 (.in(xnor_1_out));
endmodule
